// Logisim project phase 3.circ as structural Verilog: 1 circuit, main circuit main
module main (
  input  A,
  input  B,
  input  C,
  output out,
  output Change
);

  wire or_1_out;

  or or_1 (or_1_out, A, B);
  and and_1 (Change, A, B, C);
  and and_2 (out, C, or_1_out);

  // Notes on the sheet:
  //   5
  //   5
  //   10
endmodule
